// Logisim project full_adder_gate_level.circ as structural Verilog: 1 circuit, main circuit FullAdder
module FullAdder (
  input  A,
  input  B,
  input  CIN,
  output SUM,
  output COUT
);

  wire and_1_out, and_2_out, xor_1_out;

  // XOR_Gate xor_1 has open pins: out=xor_1_out
  and and_1 (and_1_out, A, B);
  // XOR_Gate xor_2 has open pins: out=SUM
  and and_2 (and_2_out, xor_1_out, CIN);
  or or_1 (COUT, and_1_out, and_2_out);
endmodule
