// Logisim project mux.circ as structural Verilog: 1 circuit, main circuit main
module main (
  input  in_1,
  input  in_2,
  input  in_3,
  input  in_4,
  output out_5,
  output out_6
);

  Multiplexer multiplexer_1 (.in0(in_1), .in1(in_2), .out(out_5), .sel(in_3), .en(in_4));
  Multiplexer multiplexer_2 (.in0(in_1), .in1(in_2), .out(out_6), .sel(in_4), .en(in_3));
endmodule
