// Logisim project splitter.circ as structural Verilog: 1 circuit, main circuit main
module main (
  input  in_1,
  output out_2,
  output out_3,
  output out_4,
  output out_5,
  output out_6,
  output out_7,
  output out_8,
  output out_9
);

  // Pins of 1 and 2 bits meet at {out_3, in_1}

  assign out_2 = in_1;
  assign out_6 = in_1;
  assign out_7 = out_3;
endmodule
