// Logisim project adder.circ as structural Verilog: 1 circuit, main circuit main
module main (
  input  in_1,
  input  in_2,
  input  in_3,
  input  in_4,
  output out_5
);

  wire [7:1] adder_1_out, undriven, undriven_2;

  Adder adder_1 (.a({undriven, in_2}), .b({undriven_2, in_3}), .out({adder_1_out, out_5}), .cin(in_1), .cout(in_4));
  // Pins of 1 and 8 bits meet at {adder_1_out, out_5}
  // Pins of 1 and 8 bits meet at {undriven, in_2}
  // Pins of 1 and 8 bits meet at {undriven_2, in_3}
endmodule
