// Logisim project button.circ as structural Verilog: 1 circuit, main circuit main
module main (
  output out_1
);

  wire button_1_out, button_2_out;

  Button button_1 (.out(button_1_out));
  not not_1 (out_1, button_1_out);
  Button button_2 (.out(button_2_out));
  not not_2 (out_1, button_2_out);
endmodule
