// Logisim project draft.circ as structural Verilog: 1 circuit, main circuit main
module main (
  input  I1,
  input  I2,
  input  I3,
  input  I4,
  input  I5,
  input  I6,
  input  I7,
  input  I8,
  input  I9,
  output D3,
  output D2,
  output D1,
  output D0
);

  wire and_1_out, and_2_out, and_3_out, and_4_out, and_5_out, and_6_out, and_7_out, not_1_out, not_2_out,
       not_3_out, not_4_out, not_5_out, not_6_out, not_7_out, or_1_out, or_2_out, or_3_out, or_4_out,
       or_5_out, or_6_out, or_7_out, or_8_out, or_9_out, or_10_out;

  or or_1 (or_1_out, I2, I3, I4, I5, I6, I7, I8, I9);
  or or_2 (or_2_out, I3, I4, I5, I6, I7, I8, I9);
  or or_3 (or_3_out, I4, I5, I6, I7, I8, I9);
  or or_4 (or_4_out, I5, I6, I7, I8, I9);
  or or_5 (or_5_out, I6, I7, I8, I9);
  or or_6 (or_6_out, I7, I8, I9);
  or or_7 (or_7_out, I8, I9);
  not not_1 (not_1_out, or_1_out);
  not not_2 (not_2_out, or_2_out);
  not not_3 (not_3_out, or_3_out);
  not not_4 (not_4_out, or_4_out);
  not not_5 (not_5_out, or_5_out);
  not not_6 (not_6_out, or_6_out);
  not not_7 (not_7_out, or_7_out);
  and and_1 (and_1_out, I1, not_1_out);
  and and_2 (and_2_out, I2, not_2_out);
  and and_3 (and_3_out, I3, not_3_out);
  and and_4 (and_4_out, I4, not_4_out);
  and and_5 (and_5_out, I5, not_5_out);
  and and_6 (and_6_out, I6, not_6_out);
  and and_7 (and_7_out, I7, not_7_out);
  not not_8 (D3, or_7_out);
  not not_9 (D2, or_8_out);
  or or_8 (or_8_out, and_4_out, and_5_out, and_6_out, and_7_out);
  not not_10 (D1, or_9_out);
  or or_9 (or_9_out, and_2_out, and_3_out, and_6_out, and_7_out);
  or or_10 (or_10_out, and_1_out, and_3_out, and_5_out, and_7_out, I9);
  not not_11 (D0, or_10_out);
endmodule
