// Logisim project ground.circ as structural Verilog: 1 circuit, main circuit main
module main (
  input  in_1,
  output out_2
);


  assign out_2 = in_1;
  // also tied to GND on the sheet: in_1
endmodule
