// Logisim project mux_4to1.circ as structural Verilog: 1 circuit, main circuit main
module main (
  input  S1,
  input  S0,
  input  D0,
  input  D1,
  input  D2,
  input  D3,
  output Z
);

  wire and_1_out, and_2_out, and_3_out, and_4_out, not_1_out, not_2_out, undriven, undriven_2, undriven_3,
       undriven_4, undriven_5, undriven_6;

  not not_1 (not_1_out, S1);
  not not_2 (not_2_out, S0);
  and and_1 (and_1_out, undriven_5, undriven_6, D0);
  and and_2 (and_2_out, not_1_out, undriven_4, D1);
  and and_3 (and_3_out, undriven_2, not_2_out, D2);
  and and_4 (and_4_out, undriven, undriven_3, D3);
  or or_1 (Z, and_1_out, and_2_out, and_3_out, and_4_out);
endmodule
