// Logisim project hust_adder_reference.circ as structural Verilog: 7 circuits, main circuit 一位二进制半加器
module \一位二进制半加器  (
  input  \输入A ,
  input  \输入B ,
  output \和输出 ,
  output \进位输出 
);

  xor xor_1 (\和输出 , \输入A , \输入B );
  and and_1 (\进位输出 , \输入A , \输入B );
endmodule

module \一位二进制全加器  (
  input  \进位 ,
  input  in_2,
  input  in_3,
  output \和 ,
  output \进位_2 
);

  wire \一位二进制半加器_1_和输出 , \一位二进制半加器_1_进位输出 , \一位二进制半加器_2_进位输出 ;

  \一位二进制半加器  \u_一位二进制半加器_1  (.\输入A (in_2), .\输入B (in_3), .\和输出 (\一位二进制半加器_1_和输出 ), .\进位输出 (\一位二进制半加器_1_进位输出 ));
  \一位二进制半加器  \u_一位二进制半加器_2  (.\输入A (\进位 ), .\输入B (\一位二进制半加器_1_和输出 ), .\和输出 (\和 ), .\进位输出 (\一位二进制半加器_2_进位输出 ));
  or or_1 (\进位_2 , \一位二进制半加器_2_进位输出 , \一位二进制半加器_1_进位输出 );
endmodule

module \串行进位并行加法器  (
  input  C0,
  input  A1,
  input  B1,
  input  A2,
  input  B2,
  input  A3,
  input  B3,
  input  A4,
  input  B4,
  output S0,
  output S1,
  output S2,
  output S3,
  output C4
);

  wire \一位二进制全加器_1_进位_2 , \一位二进制全加器_2_进位_2 , \一位二进制全加器_3_进位_2 ;

  \一位二进制全加器  \u_一位二进制全加器_1  (.in_2(A1), .in_3(B1), .\进位 (C0), .\进位_2 (\一位二进制全加器_1_进位_2 ), .\和 (S0));
  \一位二进制全加器  \u_一位二进制全加器_2  (.in_2(A2), .in_3(B2), .\进位 (\一位二进制全加器_1_进位_2 ), .\进位_2 (\一位二进制全加器_2_进位_2 ), .\和 (S1));
  \一位二进制全加器  \u_一位二进制全加器_3  (.in_2(A3), .in_3(B3), .\进位 (\一位二进制全加器_2_进位_2 ), .\进位_2 (\一位二进制全加器_3_进位_2 ), .\和 (S2));
  \一位二进制全加器  \u_一位二进制全加器_4  (.in_2(A4), .in_3(B4), .\进位 (\一位二进制全加器_3_进位_2 ), .\进位_2 (C4), .\和 (S3));
endmodule

module \先行进位并行加法器  (
  input  C0,
  input  A0,
  input  B0,
  input  A1,
  input  B1,
  input  A2,
  input  B2,
  input  A3,
  input  B3,
  output S0,
  output S1,
  output C4,
  output S2,
  output S3
);

  wire n1_bit_fa_1_gi, n1_bit_fa_1_pi, n1_bit_fa_2_gi, n1_bit_fa_2_pi, n1_bit_fa_3_gi, n1_bit_fa_3_pi,
       n1_bit_fa_4_gi, n1_bit_fa_4_pi, n4bit_cla_1_c1, n4bit_cla_1_c2, n4bit_cla_1_c3;

  _1_bit_FA u_1_bit_fa_1 (.Bi(B0), .Si(S0), .gi(n1_bit_fa_1_gi), .pi(n1_bit_fa_1_pi), .\进位 (C0), .Ai(A0));
  _1_bit_FA u_1_bit_fa_2 (.Bi(B1), .Si(S1), .gi(n1_bit_fa_2_gi), .pi(n1_bit_fa_2_pi), .\进位 (n4bit_cla_1_c1), .Ai(A1));
  _1_bit_FA u_1_bit_fa_3 (.Bi(B2), .Si(S2), .gi(n1_bit_fa_3_gi), .pi(n1_bit_fa_3_pi), .\进位 (n4bit_cla_1_c2), .Ai(A2));
  _1_bit_FA u_1_bit_fa_4 (.Bi(B3), .Si(S3), .gi(n1_bit_fa_4_gi), .pi(n1_bit_fa_4_pi), .\进位 (n4bit_cla_1_c3), .Ai(A3));
  _4bit_CLA u_4bit_cla_1 (
    .C0(C0), .G0(n1_bit_fa_1_gi), .P0(n1_bit_fa_1_pi), .G1(n1_bit_fa_2_gi), .P1(n1_bit_fa_2_pi),
    .G2(n1_bit_fa_3_gi), .P2(n1_bit_fa_3_pi), .G3(n1_bit_fa_4_gi), .P3(n1_bit_fa_4_pi), .C1(n4bit_cla_1_c1),
    .C2(n4bit_cla_1_c2), .C3(n4bit_cla_1_c3), .C4(C4));
endmodule

module \先行进位并行加法器测试电路  (
  input  C0,
  input  A0,
  input  B0,
  input  A1,
  input  B1,
  input  A2,
  input  B2,
  input  A3,
  input  B3,
  output S0,
  output S1,
  output S2,
  output S3,
  output C4
);

  \先行进位并行加法器  \u_先行进位并行加法器_1  (
    .A0(A0), .B0(B0), .A1(A1), .B1(B1), .A2(A2), .B2(B2), .A3(A3), .B3(B3), .C0(C0), .S0(S0), .S1(S1),
    .S2(S2), .S3(S3), .C4(C4));
endmodule

module _1_bit_FA (
  input  \进位 ,
  input  Ai,
  input  Bi,
  output Si,
  output gi,
  output pi
);

  wire xor_1_out;

  xor xor_1 (xor_1_out, Ai, Bi);
  xor xor_2 (Si, \进位 , xor_1_out);
  and and_1 (gi, Ai, Bi);
  or or_1 (pi, Ai, Ai);
endmodule

module _4bit_CLA (
  input  C0,
  input  G0,
  input  P0,
  input  G1,
  input  P1,
  input  G2,
  input  P2,
  input  G3,
  input  P3,
  output C1,
  output C2,
  output C3,
  output C4
);

  wire and_1_out, and_2_out, and_3_out, and_4_out, and_5_out, and_6_out, and_7_out, and_8_out, and_9_out,
       and_10_out;

  and and_1 (and_1_out, C0, P0);
  or or_1 (C1, and_1_out, G0);
  and and_2 (and_2_out, G0, P1);
  and and_3 (and_3_out, and_1_out, P1);
  or or_2 (C2, and_2_out, G1, and_3_out);
  and and_4 (and_4_out, G1, P2);
  and and_5 (and_5_out, and_2_out, P2);
  and and_6 (and_6_out, and_3_out, P2);
  or or_3 (C3, G2, and_4_out, and_5_out, and_6_out);
  and and_7 (and_7_out, G2, P3);
  and and_8 (and_8_out, and_4_out, P3);
  and and_9 (and_9_out, and_5_out, P3);
  and and_10 (and_10_out, and_6_out, P3);
  or or_4 (C4, G3, and_7_out, and_8_out, and_9_out, and_10_out);
endmodule
