// Logisim project 16bit_alu_gate_level.circ as structural Verilog: 1 circuit, main circuit main
module main (
  input  OP2,
  input  OP1,
  input  OP0,
  input  CIN,
  input  A0,
  input  B0,
  input  A1,
  input  B1,
  input  A2,
  input  B2,
  input  A3,
  input  B3,
  input  A4,
  input  B4,
  input  A5,
  input  B5,
  input  A6,
  input  B6,
  input  A7,
  input  B7,
  input  A8,
  input  B8,
  input  A9,
  input  B9,
  input  A10,
  input  B10,
  input  A11,
  input  B11,
  input  A12,
  input  B12,
  input  A13,
  input  B13,
  input  A14,
  input  B14,
  input  A15,
  input  B15,
  output Y0,
  output Y1,
  output Y2,
  output Y3,
  output Y4,
  output Y5,
  output Y6,
  output Y7,
  output Y8,
  output Y9,
  output Y10,
  output Y11,
  output Y12,
  output Y13,
  output Y14,
  output Y15,
  output COUT,
  output BORROW,
  output ZERO,
  output NEG,
  output OVF
);

  wire ADD_OR_SUB, ANDLOGIC0, ANDLOGIC1, ANDLOGIC2, ANDLOGIC3, ANDLOGIC4, ANDLOGIC5, ANDLOGIC6, ANDLOGIC7,
       ANDLOGIC8, ANDLOGIC9, ANDLOGIC10, ANDLOGIC11, ANDLOGIC12, ANDLOGIC13, ANDLOGIC14, ANDLOGIC15, BX0,
       BX1, BX2, BX3, BX4, BX5, BX6, BX7, BX8, BX9, BX10, BX11, BX12, BX13, BX14, BX15, CARRY1, CARRY2,
       CARRY3, CARRY4, CARRY5, CARRY6, CARRY7, CARRY8, CARRY9, CARRY10, CARRY11, CARRY12, CARRY13, CARRY14,
       CARRY15, CARRY16, CPROP0, CPROP1, CPROP2, CPROP3, CPROP4, CPROP5, CPROP6, CPROP7, CPROP8, CPROP9,
       CPROP10, CPROP11, CPROP12, CPROP13, CPROP14, CPROP15, G0, G1, G2, G3, G4, G5, G6, G7, G8, G9, G10,
       G11, G12, G13, G14, G15, M1_0_0, M1_0_1, M1_0_2, M1_0_3, M1_1_0, M1_1_1, M1_1_2, M1_1_3, M1_2_0,
       M1_2_1, M1_2_2, M1_2_3, M1_3_0, M1_3_1, M1_3_2, M1_3_3, M1_4_0, M1_4_1, M1_4_2, M1_4_3, M1_5_0,
       M1_5_1, M1_5_2, M1_5_3, M1_6_0, M1_6_1, M1_6_2, M1_6_3, M1_7_0, M1_7_1, M1_7_2, M1_7_3, M1_8_0,
       M1_8_1, M1_8_2, M1_8_3, M1_9_0, M1_9_1, M1_9_2, M1_9_3, M1_10_0, M1_10_1, M1_10_2, M1_10_3, M1_11_0,
       M1_11_1, M1_11_2, M1_11_3, M1_12_0, M1_12_1, M1_12_2, M1_12_3, M1_13_0, M1_13_1, M1_13_2, M1_13_3,
       M1_14_0, M1_14_1, M1_14_2, M1_14_3, M1_15_0, M1_15_1, M1_15_2, M1_15_3, M2_0_0, M2_0_1, M2_1_0,
       M2_1_1, M2_2_0, M2_2_1, M2_3_0, M2_3_1, M2_4_0, M2_4_1, M2_5_0, M2_5_1, M2_6_0, M2_6_1, M2_7_0,
       M2_7_1, M2_8_0, M2_8_1, M2_9_0, M2_9_1, M2_10_0, M2_10_1, M2_11_0, M2_11_1, M2_12_0, M2_12_1, M2_13_0,
       M2_13_1, M2_14_0, M2_14_1, M2_15_0, M2_15_1, N_CARRY_TOP, NOP0, NOP1, NOP2, NOTA0, NOTA1, NOTA2,
       NOTA3, NOTA4, NOTA5, NOTA6, NOTA7, NOTA8, NOTA9, NOTA10, NOTA11, NOTA12, NOTA13, NOTA14, NOTA15,
       OP0_0, OP0_1, OP0_2, OP0_3, OP0_4, OP0_5, OP0_6, OP0_7, OP0_8, OP0_9, OP0_10, OP0_11, OP0_12, OP0_13,
       OP0_14, OP0_15, OP1_0, OP1_1, OP1_2, OP1_3, OP1_4, OP1_5, OP1_6, OP1_7, OP1_8, OP1_9, OP1_10, OP1_11,
       OP1_12, OP1_13, OP1_14, OP1_15, OP2_0, OP2_1, OP2_2, OP2_3, OP2_4, OP2_5, OP2_6, OP2_7, OP2_8, OP2_9,
       OP2_10, OP2_11, OP2_12, OP2_13, OP2_14, OP2_15, OP3_0, OP3_1, OP3_2, OP3_3, OP3_4, OP3_5, OP3_6,
       OP3_7, OP3_8, OP3_9, OP3_10, OP3_11, OP3_12, OP3_13, OP3_14, OP3_15, OP4_0, OP4_1, OP4_2, OP4_3,
       OP4_4, OP4_5, OP4_6, OP4_7, OP4_8, OP4_9, OP4_10, OP4_11, OP4_12, OP4_13, OP4_14, OP4_15, OP5_0,
       OP5_1, OP5_2, OP5_3, OP5_4, OP5_5, OP5_6, OP5_7, OP5_8, OP5_9, OP5_10, OP5_11, OP5_12, OP5_13, OP5_14,
       OP5_15, OP6_0, OP6_1, OP6_2, OP6_3, OP6_4, OP6_5, OP6_6, OP6_7, OP6_8, OP6_9, OP6_10, OP6_11, OP6_12,
       OP6_13, OP6_14, OP6_15, OP7_0, OP7_1, OP7_2, OP7_3, OP7_4, OP7_5, OP7_6, OP7_7, OP7_8, OP7_9, OP7_10,
       OP7_11, OP7_12, OP7_13, OP7_14, OP7_15, ORLOGIC0, ORLOGIC1, ORLOGIC2, ORLOGIC3, ORLOGIC4, ORLOGIC5,
       ORLOGIC6, ORLOGIC7, ORLOGIC8, ORLOGIC9, ORLOGIC10, ORLOGIC11, ORLOGIC12, ORLOGIC13, ORLOGIC14,
       ORLOGIC15, OVF_RAW, P0, P1, P2, P3, P4, P5, P6, P7, P8, P9, P10, P11, P12, P13, P14, P15, SEL0, SEL1,
       SEL2, SEL3, SEL4, SEL5, SEL6, SEL7, SUM0, SUM1, SUM2, SUM3, SUM4, SUM5, SUM6, SUM7, SUM8, SUM9, SUM10,
       SUM11, SUM12, SUM13, SUM14, SUM15, XORLOGIC0, XORLOGIC1, XORLOGIC2, XORLOGIC3, XORLOGIC4, XORLOGIC5,
       XORLOGIC6, XORLOGIC7, XORLOGIC8, XORLOGIC9, XORLOGIC10, XORLOGIC11, XORLOGIC12, XORLOGIC13,
       XORLOGIC14, XORLOGIC15, ZOR0_0, ZOR0_1, ZOR0_2, ZOR0_3, ZOR0_4, ZOR0_5, ZOR0_6, ZOR0_7, ZOR1_0,
       ZOR1_1, ZOR1_2, ZOR1_3, ZOR2_0, ZOR2_1, ZOR3_0;

  not not_1 (NOP0, OP0);
  xor xor_1 (BX0, B0, SEL1);
  and and_1 (ANDLOGIC0, A0, B0);
  xor xor_2 (BX1, B1, SEL1);
  and and_2 (ANDLOGIC1, A1, B1);
  xor xor_3 (BX2, B2, SEL1);
  and and_3 (ANDLOGIC2, A2, B2);
  xor xor_4 (BX3, B3, SEL1);
  and and_4 (ANDLOGIC3, A3, B3);
  xor xor_5 (BX4, B4, SEL1);
  and and_5 (ANDLOGIC4, A4, B4);
  xor xor_6 (BX5, B5, SEL1);
  and and_6 (ANDLOGIC5, A5, B5);
  xor xor_7 (BX6, B6, SEL1);
  and and_7 (ANDLOGIC6, A6, B6);
  xor xor_8 (BX7, B7, SEL1);
  and and_8 (ANDLOGIC7, A7, B7);
  xor xor_9 (BX8, B8, SEL1);
  and and_9 (ANDLOGIC8, A8, B8);
  xor xor_10 (BX9, B9, SEL1);
  and and_10 (ANDLOGIC9, A9, B9);
  xor xor_11 (BX10, B10, SEL1);
  and and_11 (ANDLOGIC10, A10, B10);
  xor xor_12 (BX11, B11, SEL1);
  and and_12 (ANDLOGIC11, A11, B11);
  xor xor_13 (BX12, B12, SEL1);
  and and_13 (ANDLOGIC12, A12, B12);
  xor xor_14 (BX13, B13, SEL1);
  and and_14 (ANDLOGIC13, A13, B13);
  xor xor_15 (BX14, B14, SEL1);
  and and_15 (ANDLOGIC14, A14, B14);
  xor xor_16 (BX15, B15, SEL1);
  and and_16 (ANDLOGIC15, A15, B15);
  not not_2 (N_CARRY_TOP, CARRY16);
  not not_3 (NOP1, OP1);
  xor xor_17 (P0, A0, BX0);
  xor xor_18 (P1, A1, BX1);
  xor xor_19 (P2, A2, BX2);
  xor xor_20 (P3, A3, BX3);
  xor xor_21 (P4, A4, BX4);
  xor xor_22 (P5, A5, BX5);
  xor xor_23 (P6, A6, BX6);
  xor xor_24 (P7, A7, BX7);
  xor xor_25 (P8, A8, BX8);
  xor xor_26 (P9, A9, BX9);
  xor xor_27 (P10, A10, BX10);
  xor xor_28 (P11, A11, BX11);
  xor xor_29 (P12, A12, BX12);
  xor xor_30 (P13, A13, BX13);
  xor xor_31 (P14, A14, BX14);
  xor xor_32 (P15, A15, BX15);
  and and_17 (COUT, SEL0, CARRY16);
  not not_4 (NOP2, OP2);
  and and_18 (G0, A0, BX0);
  and and_19 (G1, A1, BX1);
  and and_20 (G2, A2, BX2);
  and and_21 (G3, A3, BX3);
  and and_22 (G4, A4, BX4);
  and and_23 (G5, A5, BX5);
  and and_24 (G6, A6, BX6);
  and and_25 (G7, A7, BX7);
  and and_26 (G8, A8, BX8);
  and and_27 (G9, A9, BX9);
  and and_28 (G10, A10, BX10);
  and and_29 (G11, A11, BX11);
  and and_30 (G12, A12, BX12);
  and and_31 (G13, A13, BX13);
  and and_32 (G14, A14, BX14);
  and and_33 (G15, A15, BX15);
  and and_34 (BORROW, SEL1, N_CARRY_TOP);
  and and_35 (SEL0, NOP2, NOP1, NOP0);
  and and_36 (CPROP0, P0, CIN);
  and and_37 (CPROP1, P1, CARRY1);
  and and_38 (CPROP2, P2, CARRY2);
  and and_39 (CPROP3, P3, CARRY3);
  and and_40 (CPROP4, P4, CARRY4);
  and and_41 (CPROP5, P5, CARRY5);
  and and_42 (CPROP6, P6, CARRY6);
  and and_43 (CPROP7, P7, CARRY7);
  and and_44 (CPROP8, P8, CARRY8);
  and and_45 (CPROP9, P9, CARRY9);
  and and_46 (CPROP10, P10, CARRY10);
  and and_47 (CPROP11, P11, CARRY11);
  and and_48 (CPROP12, P12, CARRY12);
  and and_49 (CPROP13, P13, CARRY13);
  and and_50 (CPROP14, P14, CARRY14);
  and and_51 (CPROP15, P15, CARRY15);
  xor xor_33 (OVF_RAW, CARRY15, CARRY16);
  and and_52 (SEL1, NOP2, NOP1, OP0);
  or or_1 (CARRY1, G0, CPROP0);
  or or_2 (CARRY2, G1, CPROP1);
  or or_3 (CARRY3, G2, CPROP2);
  or or_4 (CARRY4, G3, CPROP3);
  or or_5 (CARRY5, G4, CPROP4);
  or or_6 (CARRY6, G5, CPROP5);
  or or_7 (CARRY7, G6, CPROP6);
  or or_8 (CARRY8, G7, CPROP7);
  or or_9 (CARRY9, G8, CPROP8);
  or or_10 (CARRY10, G9, CPROP9);
  or or_11 (CARRY11, G10, CPROP10);
  or or_12 (CARRY12, G11, CPROP11);
  or or_13 (CARRY13, G12, CPROP12);
  or or_14 (CARRY14, G13, CPROP13);
  or or_15 (CARRY15, G14, CPROP14);
  or or_16 (CARRY16, G15, CPROP15);
  and and_53 (OVF, OVF_RAW, ADD_OR_SUB);
  and and_54 (SEL2, NOP2, OP1, NOP0);
  xor xor_34 (SUM0, P0, CIN);
  xor xor_35 (SUM1, P1, CARRY1);
  xor xor_36 (SUM2, P2, CARRY2);
  xor xor_37 (SUM3, P3, CARRY3);
  xor xor_38 (SUM4, P4, CARRY4);
  xor xor_39 (SUM5, P5, CARRY5);
  xor xor_40 (SUM6, P6, CARRY6);
  xor xor_41 (SUM7, P7, CARRY7);
  xor xor_42 (SUM8, P8, CARRY8);
  xor xor_43 (SUM9, P9, CARRY9);
  xor xor_44 (SUM10, P10, CARRY10);
  xor xor_45 (SUM11, P11, CARRY11);
  xor xor_46 (SUM12, P12, CARRY12);
  xor xor_47 (SUM13, P13, CARRY13);
  xor xor_48 (SUM14, P14, CARRY14);
  xor xor_49 (SUM15, P15, CARRY15);
  or or_17 (ZOR0_0, Y0, Y1);
  and and_55 (SEL3, NOP2, OP1, OP0);
  and and_56 (SEL4, OP2, NOP1, NOP0);
  or or_18 (ORLOGIC0, A0, B0);
  or or_19 (ORLOGIC1, A1, B1);
  or or_20 (ORLOGIC2, A2, B2);
  or or_21 (ORLOGIC3, A3, B3);
  or or_22 (ORLOGIC4, A4, B4);
  or or_23 (ORLOGIC5, A5, B5);
  or or_24 (ORLOGIC6, A6, B6);
  or or_25 (ORLOGIC7, A7, B7);
  or or_26 (ORLOGIC8, A8, B8);
  or or_27 (ORLOGIC9, A9, B9);
  or or_28 (ORLOGIC10, A10, B10);
  or or_29 (ORLOGIC11, A11, B11);
  or or_30 (ORLOGIC12, A12, B12);
  or or_31 (ORLOGIC13, A13, B13);
  or or_32 (ORLOGIC14, A14, B14);
  or or_33 (ORLOGIC15, A15, B15);
  or or_34 (ZOR0_1, Y2, Y3);
  and and_57 (SEL5, OP2, NOP1, OP0);
  xor xor_50 (XORLOGIC0, A0, B0);
  xor xor_51 (XORLOGIC1, A1, B1);
  xor xor_52 (XORLOGIC2, A2, B2);
  xor xor_53 (XORLOGIC3, A3, B3);
  xor xor_54 (XORLOGIC4, A4, B4);
  xor xor_55 (XORLOGIC5, A5, B5);
  xor xor_56 (XORLOGIC6, A6, B6);
  xor xor_57 (XORLOGIC7, A7, B7);
  xor xor_58 (XORLOGIC8, A8, B8);
  xor xor_59 (XORLOGIC9, A9, B9);
  xor xor_60 (XORLOGIC10, A10, B10);
  xor xor_61 (XORLOGIC11, A11, B11);
  xor xor_62 (XORLOGIC12, A12, B12);
  xor xor_63 (XORLOGIC13, A13, B13);
  xor xor_64 (XORLOGIC14, A14, B14);
  xor xor_65 (XORLOGIC15, A15, B15);
  or or_35 (ZOR0_2, Y4, Y5);
  or or_36 (ZOR0_3, Y6, Y7);
  and and_58 (SEL6, OP2, OP1, NOP0);
  not not_5 (NOTA0, A0);
  not not_6 (NOTA1, A1);
  not not_7 (NOTA2, A2);
  not not_8 (NOTA3, A3);
  not not_9 (NOTA4, A4);
  not not_10 (NOTA5, A5);
  not not_11 (NOTA6, A6);
  not not_12 (NOTA7, A7);
  not not_13 (NOTA8, A8);
  not not_14 (NOTA9, A9);
  not not_15 (NOTA10, A10);
  not not_16 (NOTA11, A11);
  not not_17 (NOTA12, A12);
  not not_18 (NOTA13, A13);
  not not_19 (NOTA14, A14);
  not not_20 (NOTA15, A15);
  or or_37 (ZOR0_4, Y8, Y9);
  and and_59 (SEL7, OP2, OP1, OP0);
  and and_60 (OP0_0, SEL0, SUM0);
  and and_61 (OP0_1, SEL0, SUM1);
  and and_62 (OP0_2, SEL0, SUM2);
  and and_63 (OP0_3, SEL0, SUM3);
  and and_64 (OP0_4, SEL0, SUM4);
  and and_65 (OP0_5, SEL0, SUM5);
  and and_66 (OP0_6, SEL0, SUM6);
  and and_67 (OP0_7, SEL0, SUM7);
  and and_68 (OP0_8, SEL0, SUM8);
  and and_69 (OP0_9, SEL0, SUM9);
  and and_70 (OP0_10, SEL0, SUM10);
  and and_71 (OP0_11, SEL0, SUM11);
  and and_72 (OP0_12, SEL0, SUM12);
  and and_73 (OP0_13, SEL0, SUM13);
  and and_74 (OP0_14, SEL0, SUM14);
  and and_75 (OP0_15, SEL0, SUM15);
  or or_38 (ADD_OR_SUB, SEL0, SEL1);
  or or_39 (ZOR0_5, Y10, Y11);
  and and_76 (OP1_0, SEL1, SUM0);
  and and_77 (OP1_1, SEL1, SUM1);
  and and_78 (OP1_2, SEL1, SUM2);
  and and_79 (OP1_3, SEL1, SUM3);
  and and_80 (OP1_4, SEL1, SUM4);
  and and_81 (OP1_5, SEL1, SUM5);
  and and_82 (OP1_6, SEL1, SUM6);
  and and_83 (OP1_7, SEL1, SUM7);
  and and_84 (OP1_8, SEL1, SUM8);
  and and_85 (OP1_9, SEL1, SUM9);
  and and_86 (OP1_10, SEL1, SUM10);
  and and_87 (OP1_11, SEL1, SUM11);
  and and_88 (OP1_12, SEL1, SUM12);
  and and_89 (OP1_13, SEL1, SUM13);
  and and_90 (OP1_14, SEL1, SUM14);
  and and_91 (OP1_15, SEL1, SUM15);
  or or_40 (ZOR0_6, Y12, Y13);
  and and_92 (OP2_0, SEL2, ANDLOGIC0);
  and and_93 (OP2_1, SEL2, ANDLOGIC1);
  and and_94 (OP2_2, SEL2, ANDLOGIC2);
  and and_95 (OP2_3, SEL2, ANDLOGIC3);
  and and_96 (OP2_4, SEL2, ANDLOGIC4);
  and and_97 (OP2_5, SEL2, ANDLOGIC5);
  and and_98 (OP2_6, SEL2, ANDLOGIC6);
  and and_99 (OP2_7, SEL2, ANDLOGIC7);
  and and_100 (OP2_8, SEL2, ANDLOGIC8);
  and and_101 (OP2_9, SEL2, ANDLOGIC9);
  and and_102 (OP2_10, SEL2, ANDLOGIC10);
  and and_103 (OP2_11, SEL2, ANDLOGIC11);
  and and_104 (OP2_12, SEL2, ANDLOGIC12);
  and and_105 (OP2_13, SEL2, ANDLOGIC13);
  and and_106 (OP2_14, SEL2, ANDLOGIC14);
  and and_107 (OP2_15, SEL2, ANDLOGIC15);
  or or_41 (ZOR0_7, Y14, NEG);
  and and_108 (OP3_0, SEL3, ORLOGIC0);
  and and_109 (OP3_1, SEL3, ORLOGIC1);
  and and_110 (OP3_2, SEL3, ORLOGIC2);
  and and_111 (OP3_3, SEL3, ORLOGIC3);
  and and_112 (OP3_4, SEL3, ORLOGIC4);
  and and_113 (OP3_5, SEL3, ORLOGIC5);
  and and_114 (OP3_6, SEL3, ORLOGIC6);
  and and_115 (OP3_7, SEL3, ORLOGIC7);
  and and_116 (OP3_8, SEL3, ORLOGIC8);
  and and_117 (OP3_9, SEL3, ORLOGIC9);
  and and_118 (OP3_10, SEL3, ORLOGIC10);
  and and_119 (OP3_11, SEL3, ORLOGIC11);
  and and_120 (OP3_12, SEL3, ORLOGIC12);
  and and_121 (OP3_13, SEL3, ORLOGIC13);
  and and_122 (OP3_14, SEL3, ORLOGIC14);
  and and_123 (OP3_15, SEL3, ORLOGIC15);
  or or_42 (ZOR1_0, ZOR0_0, ZOR0_1);
  and and_124 (OP4_0, SEL4, XORLOGIC0);
  and and_125 (OP4_1, SEL4, XORLOGIC1);
  and and_126 (OP4_2, SEL4, XORLOGIC2);
  and and_127 (OP4_3, SEL4, XORLOGIC3);
  and and_128 (OP4_4, SEL4, XORLOGIC4);
  and and_129 (OP4_5, SEL4, XORLOGIC5);
  and and_130 (OP4_6, SEL4, XORLOGIC6);
  and and_131 (OP4_7, SEL4, XORLOGIC7);
  and and_132 (OP4_8, SEL4, XORLOGIC8);
  and and_133 (OP4_9, SEL4, XORLOGIC9);
  and and_134 (OP4_10, SEL4, XORLOGIC10);
  and and_135 (OP4_11, SEL4, XORLOGIC11);
  and and_136 (OP4_12, SEL4, XORLOGIC12);
  and and_137 (OP4_13, SEL4, XORLOGIC13);
  and and_138 (OP4_14, SEL4, XORLOGIC14);
  and and_139 (OP4_15, SEL4, XORLOGIC15);
  or or_43 (ZOR1_1, ZOR0_2, ZOR0_3);
  and and_140 (OP5_0, SEL5, NOTA0);
  and and_141 (OP5_1, SEL5, NOTA1);
  and and_142 (OP5_2, SEL5, NOTA2);
  and and_143 (OP5_3, SEL5, NOTA3);
  and and_144 (OP5_4, SEL5, NOTA4);
  and and_145 (OP5_5, SEL5, NOTA5);
  and and_146 (OP5_6, SEL5, NOTA6);
  and and_147 (OP5_7, SEL5, NOTA7);
  and and_148 (OP5_8, SEL5, NOTA8);
  and and_149 (OP5_9, SEL5, NOTA9);
  and and_150 (OP5_10, SEL5, NOTA10);
  and and_151 (OP5_11, SEL5, NOTA11);
  and and_152 (OP5_12, SEL5, NOTA12);
  and and_153 (OP5_13, SEL5, NOTA13);
  and and_154 (OP5_14, SEL5, NOTA14);
  and and_155 (OP5_15, SEL5, NOTA15);
  or or_44 (ZOR1_2, ZOR0_4, ZOR0_5);
  and and_156 (OP6_0, SEL6, CIN);
  and and_157 (OP6_1, SEL6, A0);
  and and_158 (OP6_2, SEL6, A1);
  and and_159 (OP6_3, SEL6, A2);
  and and_160 (OP6_4, SEL6, A3);
  and and_161 (OP6_5, SEL6, A4);
  and and_162 (OP6_6, SEL6, A5);
  and and_163 (OP6_7, SEL6, A6);
  and and_164 (OP6_8, SEL6, A7);
  and and_165 (OP6_9, SEL6, A8);
  and and_166 (OP6_10, SEL6, A9);
  and and_167 (OP6_11, SEL6, A10);
  and and_168 (OP6_12, SEL6, A11);
  and and_169 (OP6_13, SEL6, A12);
  and and_170 (OP6_14, SEL6, A13);
  and and_171 (OP6_15, SEL6, A14);
  or or_45 (ZOR1_3, ZOR0_6, ZOR0_7);
  and and_172 (OP7_0, SEL7, A1);
  and and_173 (OP7_1, SEL7, A2);
  and and_174 (OP7_2, SEL7, A3);
  and and_175 (OP7_3, SEL7, A4);
  and and_176 (OP7_4, SEL7, A5);
  and and_177 (OP7_5, SEL7, A6);
  and and_178 (OP7_6, SEL7, A7);
  and and_179 (OP7_7, SEL7, A8);
  and and_180 (OP7_8, SEL7, A9);
  and and_181 (OP7_9, SEL7, A10);
  and and_182 (OP7_10, SEL7, A11);
  and and_183 (OP7_11, SEL7, A12);
  and and_184 (OP7_12, SEL7, A13);
  and and_185 (OP7_13, SEL7, A14);
  and and_186 (OP7_14, SEL7, A15);
  and and_187 (OP7_15, SEL7, CIN);
  or or_46 (ZOR2_0, ZOR1_0, ZOR1_1);
  or or_47 (M1_0_0, OP0_0, OP1_0);
  or or_48 (M1_1_0, OP0_1, OP1_1);
  or or_49 (M1_2_0, OP0_2, OP1_2);
  or or_50 (M1_3_0, OP0_3, OP1_3);
  or or_51 (M1_4_0, OP0_4, OP1_4);
  or or_52 (M1_5_0, OP0_5, OP1_5);
  or or_53 (M1_6_0, OP0_6, OP1_6);
  or or_54 (M1_7_0, OP0_7, OP1_7);
  or or_55 (M1_8_0, OP0_8, OP1_8);
  or or_56 (M1_9_0, OP0_9, OP1_9);
  or or_57 (M1_10_0, OP0_10, OP1_10);
  or or_58 (M1_11_0, OP0_11, OP1_11);
  or or_59 (M1_12_0, OP0_12, OP1_12);
  or or_60 (M1_13_0, OP0_13, OP1_13);
  or or_61 (M1_14_0, OP0_14, OP1_14);
  or or_62 (M1_15_0, OP0_15, OP1_15);
  or or_63 (ZOR2_1, ZOR1_2, ZOR1_3);
  or or_64 (M1_0_1, OP2_0, OP3_0);
  or or_65 (M1_1_1, OP2_1, OP3_1);
  or or_66 (M1_2_1, OP2_2, OP3_2);
  or or_67 (M1_3_1, OP2_3, OP3_3);
  or or_68 (M1_4_1, OP2_4, OP3_4);
  or or_69 (M1_5_1, OP2_5, OP3_5);
  or or_70 (M1_6_1, OP2_6, OP3_6);
  or or_71 (M1_7_1, OP2_7, OP3_7);
  or or_72 (M1_8_1, OP2_8, OP3_8);
  or or_73 (M1_9_1, OP2_9, OP3_9);
  or or_74 (M1_10_1, OP2_10, OP3_10);
  or or_75 (M1_11_1, OP2_11, OP3_11);
  or or_76 (M1_12_1, OP2_12, OP3_12);
  or or_77 (M1_13_1, OP2_13, OP3_13);
  or or_78 (M1_14_1, OP2_14, OP3_14);
  or or_79 (M1_15_1, OP2_15, OP3_15);
  or or_80 (ZOR3_0, ZOR2_0, ZOR2_1);
  or or_81 (M1_0_2, OP4_0, OP5_0);
  or or_82 (M1_1_2, OP4_1, OP5_1);
  or or_83 (M1_2_2, OP4_2, OP5_2);
  or or_84 (M1_3_2, OP4_3, OP5_3);
  or or_85 (M1_4_2, OP4_4, OP5_4);
  or or_86 (M1_5_2, OP4_5, OP5_5);
  or or_87 (M1_6_2, OP4_6, OP5_6);
  or or_88 (M1_7_2, OP4_7, OP5_7);
  or or_89 (M1_8_2, OP4_8, OP5_8);
  or or_90 (M1_9_2, OP4_9, OP5_9);
  or or_91 (M1_10_2, OP4_10, OP5_10);
  or or_92 (M1_11_2, OP4_11, OP5_11);
  or or_93 (M1_12_2, OP4_12, OP5_12);
  or or_94 (M1_13_2, OP4_13, OP5_13);
  or or_95 (M1_14_2, OP4_14, OP5_14);
  or or_96 (M1_15_2, OP4_15, OP5_15);
  not not_21 (ZERO, ZOR3_0);
  or or_97 (M1_0_3, OP6_0, OP7_0);
  or or_98 (M1_1_3, OP6_1, OP7_1);
  or or_99 (M1_2_3, OP6_2, OP7_2);
  or or_100 (M1_3_3, OP6_3, OP7_3);
  or or_101 (M1_4_3, OP6_4, OP7_4);
  or or_102 (M1_5_3, OP6_5, OP7_5);
  or or_103 (M1_6_3, OP6_6, OP7_6);
  or or_104 (M1_7_3, OP6_7, OP7_7);
  or or_105 (M1_8_3, OP6_8, OP7_8);
  or or_106 (M1_9_3, OP6_9, OP7_9);
  or or_107 (M1_10_3, OP6_10, OP7_10);
  or or_108 (M1_11_3, OP6_11, OP7_11);
  or or_109 (M1_12_3, OP6_12, OP7_12);
  or or_110 (M1_13_3, OP6_13, OP7_13);
  or or_111 (M1_14_3, OP6_14, OP7_14);
  or or_112 (M1_15_3, OP6_15, OP7_15);
  or or_113 (M2_0_0, M1_0_0, M1_0_1);
  or or_114 (M2_1_0, M1_1_0, M1_1_1);
  or or_115 (M2_2_0, M1_2_0, M1_2_1);
  or or_116 (M2_3_0, M1_3_0, M1_3_1);
  or or_117 (M2_4_0, M1_4_0, M1_4_1);
  or or_118 (M2_5_0, M1_5_0, M1_5_1);
  or or_119 (M2_6_0, M1_6_0, M1_6_1);
  or or_120 (M2_7_0, M1_7_0, M1_7_1);
  or or_121 (M2_8_0, M1_8_0, M1_8_1);
  or or_122 (M2_9_0, M1_9_0, M1_9_1);
  or or_123 (M2_10_0, M1_10_0, M1_10_1);
  or or_124 (M2_11_0, M1_11_0, M1_11_1);
  or or_125 (M2_12_0, M1_12_0, M1_12_1);
  or or_126 (M2_13_0, M1_13_0, M1_13_1);
  or or_127 (M2_14_0, M1_14_0, M1_14_1);
  or or_128 (M2_15_0, M1_15_0, M1_15_1);
  or or_129 (M2_0_1, M1_0_2, M1_0_3);
  or or_130 (M2_1_1, M1_1_2, M1_1_3);
  or or_131 (M2_2_1, M1_2_2, M1_2_3);
  or or_132 (M2_3_1, M1_3_2, M1_3_3);
  or or_133 (M2_4_1, M1_4_2, M1_4_3);
  or or_134 (M2_5_1, M1_5_2, M1_5_3);
  or or_135 (M2_6_1, M1_6_2, M1_6_3);
  or or_136 (M2_7_1, M1_7_2, M1_7_3);
  or or_137 (M2_8_1, M1_8_2, M1_8_3);
  or or_138 (M2_9_1, M1_9_2, M1_9_3);
  or or_139 (M2_10_1, M1_10_2, M1_10_3);
  or or_140 (M2_11_1, M1_11_2, M1_11_3);
  or or_141 (M2_12_1, M1_12_2, M1_12_3);
  or or_142 (M2_13_1, M1_13_2, M1_13_3);
  or or_143 (M2_14_1, M1_14_2, M1_14_3);
  or or_144 (M2_15_1, M1_15_2, M1_15_3);
  or or_145 (Y0, M2_0_0, M2_0_1);
  or or_146 (Y1, M2_1_0, M2_1_1);
  or or_147 (Y2, M2_2_0, M2_2_1);
  or or_148 (Y3, M2_3_0, M2_3_1);
  or or_149 (Y4, M2_4_0, M2_4_1);
  or or_150 (Y5, M2_5_0, M2_5_1);
  or or_151 (Y6, M2_6_0, M2_6_1);
  or or_152 (Y7, M2_7_0, M2_7_1);
  or or_153 (Y8, M2_8_0, M2_8_1);
  or or_154 (Y9, M2_9_0, M2_9_1);
  or or_155 (Y10, M2_10_0, M2_10_1);
  or or_156 (Y11, M2_11_0, M2_11_1);
  or or_157 (Y12, M2_12_0, M2_12_1);
  or or_158 (Y13, M2_13_0, M2_13_1);
  or or_159 (Y14, M2_14_0, M2_14_1);
  or or_160 (NEG, M2_15_0, M2_15_1);

  assign Y15 = NEG;

  // Notes on the sheet:
  //   OP2..0: 000 ADD  001 SUB  010 AND  011 OR  100 XOR  101 NOT-A  110 SHL  111 SHR
  //   CIN: ADD carry input; SUB borrow input is active low (1 = no incoming borrow).
  //   ARITHMETIC
  //   FLAGS
  //   ONE-HOT RESULT MUX
  //   OUTPUTS
endmodule
