// Logisim project keypad_priority_encoder_flat_direct.circ as structural Verilog: 1 circuit, main circuit main
module main (
  input  K9,
  input  K8,
  input  K7,
  input  K6,
  input  K5,
  input  K4,
  input  K3,
  input  K2,
  input  K1,
  input  K0,
  output B0,
  output B1,
  output B2,
  output B3,
  output VALID
);

  wire and_1_out, and_2_out, and_3_out, and_4_out, and_5_out, and_6_out, and_7_out, and_8_out, not_1_out,
       not_2_out, not_3_out, not_4_out, not_5_out, not_6_out, not_7_out, not_8_out, or_1_out, or_2_out,
       or_3_out, or_4_out, or_5_out, or_6_out, or_7_out, or_8_out;

  or or_1 (or_1_out, K9, K8);
  or or_2 (or_2_out, or_1_out, K7);
  or or_3 (or_3_out, or_2_out, K6);
  or or_4 (or_4_out, or_3_out, K5);
  or or_5 (or_5_out, or_4_out, K4);
  or or_6 (or_6_out, or_5_out, K3);
  or or_7 (or_7_out, or_6_out, K2);
  or or_8 (or_8_out, or_7_out, K1);
  or or_9 (VALID, or_8_out, K0);
  not not_1 (not_1_out, K9);
  not not_2 (not_2_out, or_1_out);
  not not_3 (not_3_out, or_2_out);
  not not_4 (not_4_out, or_3_out);
  not not_5 (not_5_out, or_4_out);
  not not_6 (not_6_out, or_5_out);
  not not_7 (not_7_out, or_6_out);
  not not_8 (not_8_out, or_7_out);
  and and_1 (and_1_out, not_1_out, K8);
  and and_2 (and_2_out, not_2_out, K7);
  and and_3 (and_3_out, not_3_out, K6);
  and and_4 (and_4_out, not_4_out, K5);
  and and_5 (and_5_out, not_5_out, K4);
  and and_6 (and_6_out, not_6_out, K3);
  and and_7 (and_7_out, not_7_out, K2);
  and and_8 (and_8_out, not_8_out, K1);
  or or_10 (B0, K9, and_2_out, and_4_out, and_6_out, and_8_out);
  or or_11 (B1, and_2_out, and_3_out, and_6_out, and_7_out);
  or or_12 (B2, and_2_out, and_3_out, and_4_out, and_5_out);
  or or_13 (B3, and_1_out, K9);

  // Notes on the sheet:
  //   DECIMAL KEYPAD PRIORITY ENCODER - FLAT DIRECT-WIRE VERSION
  //   K9 highest priority; no subcircuits and no Tunnels.
  //   SUFFIX PRIORITY
  //   HIGHER-KEY SUPPRESSION
  //   ONE-HOT TERMS
  //   BCD OUTPUT
endmodule
