// Logisim project keypad_priority_encoder_hierarchical.circ as structural Verilog: 4 circuits, main circuit main
module PriorityStage (
  input  K9,
  input  K8,
  input  K7,
  input  K6,
  input  K5,
  input  K4,
  input  K3,
  input  K2,
  input  K1,
  input  K0,
  output K9_2,
  output H8,
  output K8_2,
  output H7,
  output K7_2,
  output H6,
  output K6_2,
  output H5,
  output K5_2,
  output H4,
  output K4_2,
  output H3,
  output K3_2,
  output H2,
  output K2_2,
  output H1,
  output K1_2,
  output VALID
);

  wire or_1_out, or_2_out, or_3_out, or_4_out, or_5_out, or_6_out, or_7_out, or_8_out;

  or or_1 (or_1_out, K9, K8);
  or or_2 (or_2_out, or_1_out, K7);
  or or_3 (or_3_out, or_2_out, K6);
  or or_4 (or_4_out, or_3_out, K5);
  or or_5 (or_5_out, or_4_out, K4);
  or or_6 (or_6_out, or_5_out, K3);
  or or_7 (or_7_out, or_6_out, K2);
  or or_8 (or_8_out, or_7_out, K1);
  or or_9 (VALID, or_8_out, K0);
  not not_1 (H8, K9);
  not not_2 (H7, or_1_out);
  not not_3 (H6, or_2_out);
  not not_4 (H5, or_3_out);
  not not_5 (H4, or_4_out);
  not not_6 (H3, or_5_out);
  not not_7 (H2, or_6_out);
  not not_8 (H1, or_7_out);

  assign K1_2 = K1;
  assign K2_2 = K2;
  assign K3_2 = K3;
  assign K4_2 = K4;
  assign K5_2 = K5;
  assign K6_2 = K6;
  assign K7_2 = K7;
  assign K8_2 = K8;
  assign K9_2 = K9;
endmodule

module TermStage (
  input  K1,
  input  H1,
  input  K2,
  input  H2,
  input  K3,
  input  H3,
  input  K4,
  input  H4,
  input  K5,
  input  H5,
  input  K6,
  input  H6,
  input  K7,
  input  H7,
  input  K8,
  input  H8,
  input  K9,
  output T1,
  output T2,
  output T3,
  output T4,
  output T5,
  output T6,
  output T7,
  output T8,
  output T9
);

  and and_1 (T1, K1, H1);
  and and_2 (T2, K2, H2);
  and and_3 (T3, K3, H3);
  and and_4 (T4, K4, H4);
  and and_5 (T5, K5, H5);
  and and_6 (T6, K6, H6);
  and and_7 (T7, K7, H7);
  and and_8 (T8, K8, H8);

  assign T9 = K9;
endmodule

module BCDStage (
  input  T1,
  input  T2,
  input  T3,
  input  T4,
  input  T5,
  input  T6,
  input  T7,
  input  T8,
  input  T9,
  output B0,
  output B1,
  output B2,
  output B3
);

  or or_1 (B0, T1, T3, T5, T7, T9);
  or or_2 (B1, T2, T3, T6, T7);
  or or_3 (B2, T4, T5, T6, T7);
  or or_4 (B3, T8, T9);
endmodule

module main (
  input  K0,
  input  K1,
  input  K2,
  input  K3,
  input  K4,
  input  K5,
  input  K6,
  input  K7,
  input  K8,
  input  K9,
  output B0,
  output B1,
  output B2,
  output B3,
  output VALID
);

  wire PriorityStage_h1, PriorityStage_h2, PriorityStage_h3, PriorityStage_h4, PriorityStage_h5,
       PriorityStage_h6, PriorityStage_h7, PriorityStage_h8, PriorityStage_k1_2, PriorityStage_k2_2,
       PriorityStage_k3_2, PriorityStage_k4_2, PriorityStage_k5_2, PriorityStage_k6_2, PriorityStage_k7_2,
       PriorityStage_k8_2, PriorityStage_k9_2, TermStage_t1, TermStage_t2, TermStage_t3, TermStage_t4,
       TermStage_t5, TermStage_t6, TermStage_t7, TermStage_t8, TermStage_t9;

  PriorityStage PriorityStage (
    .K0(K0), .K1(K1), .K2(K2), .K3(K3), .K4(K4), .K5(K5), .K6(K6), .K7(K7), .K8(K8), .K9(K9),
    .K1_2(PriorityStage_k1_2), .K2_2(PriorityStage_k2_2), .K3_2(PriorityStage_k3_2),
    .K4_2(PriorityStage_k4_2), .K5_2(PriorityStage_k5_2), .K6_2(PriorityStage_k6_2),
    .K7_2(PriorityStage_k7_2), .K8_2(PriorityStage_k8_2), .K9_2(PriorityStage_k9_2), .H1(PriorityStage_h1),
    .H2(PriorityStage_h2), .H3(PriorityStage_h3), .H4(PriorityStage_h4), .H5(PriorityStage_h5),
    .H6(PriorityStage_h6), .H7(PriorityStage_h7), .H8(PriorityStage_h8), .VALID(VALID));
  TermStage TermStage (
    .K1(PriorityStage_k1_2), .K2(PriorityStage_k2_2), .K3(PriorityStage_k3_2), .K4(PriorityStage_k4_2),
    .K5(PriorityStage_k5_2), .K6(PriorityStage_k6_2), .K7(PriorityStage_k7_2), .K8(PriorityStage_k8_2),
    .K9(PriorityStage_k9_2), .H1(PriorityStage_h1), .H2(PriorityStage_h2), .H3(PriorityStage_h3),
    .H4(PriorityStage_h4), .H5(PriorityStage_h5), .H6(PriorityStage_h6), .H7(PriorityStage_h7),
    .H8(PriorityStage_h8), .T1(TermStage_t1), .T2(TermStage_t2), .T3(TermStage_t3), .T4(TermStage_t4),
    .T5(TermStage_t5), .T6(TermStage_t6), .T7(TermStage_t7), .T8(TermStage_t8), .T9(TermStage_t9));
  BCDStage BCDStage (
    .T1(TermStage_t1), .T2(TermStage_t2), .T3(TermStage_t3), .T4(TermStage_t4), .T5(TermStage_t5),
    .T6(TermStage_t6), .T7(TermStage_t7), .T8(TermStage_t8), .T9(TermStage_t9), .B0(B0), .B1(B1), .B2(B2),
    .B3(B3));

  // Notes on the sheet:
  //   DECIMAL KEYPAD PRIORITY ENCODER - HIERARCHICAL DIRECT-WIRE VERSION
  //   No Tunnels. PriorityStage -> TermStage -> BCDStage.
endmodule
