// Logisim project encoder_8to3_gate_level.circ as structural Verilog: 1 circuit, main circuit main
module main (
  input  I7,
  input  I6,
  input  I5,
  input  I4,
  input  I3,
  input  I2,
  input  I1,
  input  I0,
  output Y0,
  output Y1,
  output Y2,
  output VALID
);

  wire and_1_out, and_2_out, and_3_out, and_4_out, and_5_out, and_6_out, not_1_out, not_2_out, not_3_out,
       not_4_out, not_5_out, not_6_out, or_1_out, or_2_out, or_3_out, or_4_out, or_5_out, or_6_out;

  or or_1 (or_1_out, I7, I6);
  or or_2 (or_2_out, or_1_out, I5);
  or or_3 (or_3_out, or_2_out, I4);
  or or_4 (or_4_out, or_3_out, I3);
  or or_5 (or_5_out, or_4_out, I2);
  or or_6 (or_6_out, or_5_out, I1);
  or or_7 (VALID, or_6_out, I0);
  not not_1 (not_1_out, I7);
  not not_2 (not_2_out, or_1_out);
  not not_3 (not_3_out, or_2_out);
  not not_4 (not_4_out, or_3_out);
  not not_5 (not_5_out, or_4_out);
  not not_6 (not_6_out, or_5_out);
  and and_1 (and_1_out, not_1_out, I6);
  and and_2 (and_2_out, not_2_out, I5);
  and and_3 (and_3_out, not_3_out, I4);
  and and_4 (and_4_out, not_4_out, I3);
  and and_5 (and_5_out, not_5_out, I2);
  and and_6 (and_6_out, not_6_out, I1);
  or or_8 (Y0, I7, and_2_out, and_4_out, and_6_out);
  or or_9 (Y1, I7, and_1_out, and_4_out, and_5_out);
  or or_10 (Y2, I7, and_1_out, and_2_out, and_3_out);

  // Notes on the sheet:
  //   8-TO-3 PRIORITY ENCODER
  //   I7 highest priority; Y2..Y0 binary digit; VALID detects any input.
endmodule
