// Logisim project 4x4_array_multiplier_gate_level.circ as structural Verilog: 1 circuit, main circuit main
module main (
  input  A0,
  input  A1,
  input  A2,
  input  A3,
  input  B0,
  input  B1,
  input  B2,
  input  B3,
  output P0,
  output P1,
  output P2,
  output P3,
  output P4,
  output P5,
  output P6,
  output P7
);

  wire and_2_out, and_3_out, and_4_out, and_5_out, and_6_out, and_7_out, and_8_out, and_9_out, and_10_out,
       and_11_out, and_12_out, and_13_out, and_14_out, and_15_out, and_16_out, and_17_out, and_18_out,
       and_19_out, and_20_out, and_21_out, and_22_out, and_23_out, and_24_out, and_25_out, and_26_out,
       and_27_out, and_28_out, and_29_out, and_30_out, and_31_out, and_32_out, and_33_out, and_34_out,
       and_35_out, and_36_out, or_1_out, or_2_out, or_3_out, or_4_out, or_5_out, or_6_out, or_7_out,
       xor_2_out, xor_4_out, xor_5_out, xor_6_out, xor_8_out, xor_9_out, xor_10_out, xor_11_out, xor_12_out,
       xor_13_out, xor_15_out, xor_16_out, xor_17_out, xor_19_out;

  and and_1 (P0, A0, B0);
  and and_2 (and_2_out, A0, B1);
  and and_3 (and_3_out, A0, B2);
  and and_4 (and_4_out, A0, B3);
  and and_5 (and_5_out, A1, B0);
  and and_6 (and_6_out, A1, B1);
  and and_7 (and_7_out, A1, B2);
  and and_8 (and_8_out, A1, B3);
  and and_9 (and_9_out, A2, B0);
  and and_10 (and_10_out, A2, B1);
  and and_11 (and_11_out, A2, B2);
  and and_12 (and_12_out, A2, B3);
  and and_13 (and_13_out, A3, B0);
  and and_14 (and_14_out, A3, B1);
  and and_15 (and_15_out, A3, B2);
  and and_16 (and_16_out, A3, B3);
  xor xor_1 (P1, and_2_out, and_5_out);
  and and_17 (and_17_out, and_2_out, and_5_out);
  xor xor_2 (xor_2_out, and_6_out, and_9_out);
  and and_18 (and_18_out, and_6_out, and_9_out);
  xor xor_3 (P2, and_3_out, xor_4_out);
  and and_19 (and_19_out, and_3_out, xor_4_out);
  xor xor_4 (xor_4_out, xor_2_out, and_17_out);
  and and_20 (and_20_out, xor_2_out, and_17_out);
  or or_1 (or_1_out, and_18_out, and_20_out);
  xor xor_5 (xor_5_out, and_10_out, and_13_out);
  and and_21 (and_21_out, and_10_out, and_13_out);
  xor xor_6 (xor_6_out, and_7_out, xor_8_out);
  and and_22 (and_22_out, and_7_out, xor_8_out);
  xor xor_7 (P3, and_4_out, xor_9_out);
  and and_23 (and_23_out, and_4_out, xor_9_out);
  xor xor_8 (xor_8_out, xor_5_out, or_1_out);
  and and_24 (and_24_out, xor_5_out, or_1_out);
  xor xor_9 (xor_9_out, xor_6_out, and_19_out);
  and and_25 (and_25_out, xor_6_out, and_19_out);
  or or_2 (or_2_out, and_21_out, and_24_out);
  or or_3 (or_3_out, and_22_out, and_25_out);
  xor xor_10 (xor_10_out, and_14_out, or_2_out);
  and and_26 (and_26_out, and_14_out, or_2_out);
  xor xor_11 (xor_11_out, and_11_out, xor_10_out);
  and and_27 (and_27_out, and_11_out, xor_10_out);
  xor xor_12 (xor_12_out, and_8_out, xor_13_out);
  and and_28 (and_28_out, and_8_out, xor_13_out);
  xor xor_13 (xor_13_out, xor_11_out, or_3_out);
  and and_29 (and_29_out, xor_11_out, or_3_out);
  xor xor_14 (P4, xor_12_out, and_23_out);
  and and_30 (and_30_out, xor_12_out, and_23_out);
  or or_4 (or_4_out, and_27_out, and_29_out);
  or or_5 (or_5_out, and_28_out, and_30_out);
  xor xor_15 (xor_15_out, and_15_out, and_26_out);
  and and_31 (and_31_out, and_15_out, and_26_out);
  xor xor_16 (xor_16_out, and_12_out, xor_17_out);
  and and_32 (and_32_out, and_12_out, xor_17_out);
  xor xor_17 (xor_17_out, xor_15_out, or_4_out);
  and and_33 (and_33_out, xor_15_out, or_4_out);
  xor xor_18 (P5, xor_16_out, or_5_out);
  and and_34 (and_34_out, xor_16_out, or_5_out);
  or or_6 (or_6_out, and_31_out, and_33_out);
  or or_7 (or_7_out, and_32_out, and_34_out);
  xor xor_19 (xor_19_out, and_16_out, or_6_out);
  and and_35 (and_35_out, and_16_out, or_6_out);
  xor xor_20 (P6, xor_19_out, or_7_out);
  and and_36 (and_36_out, xor_19_out, or_7_out);
  or or_8 (P7, and_35_out, and_36_out);

  // Notes on the sheet:
  //   4x4 ARRAY MULTIPLIER - GATE-LEVEL DIRECT-WIRE
  //   PARTIAL PRODUCTS: PPij = Ai AND Bj
  //   ACCUMULATION ROW B1
  //   ACCUMULATION ROW B2
  //   ACCUMULATION ROW B3
  //   8-BIT PRODUCT
endmodule
