// Logisim project stress_256_gate_level.circ as structural Verilog: 1 circuit, main circuit main
module main (
  input  I0,
  input  I8,
  input  I1,
  input  I9,
  input  I2,
  input  I10,
  input  I3,
  input  I11,
  input  I4,
  input  I12,
  input  I5,
  input  I13,
  input  I6,
  input  I14,
  input  I7,
  input  I15,
  output O0,
  output O1,
  output O2,
  output O3
);

  wire and_1_out, and_2_out, and_3_out, and_4_out, and_5_out, and_6_out, and_7_out, and_8_out, and_9_out,
       and_10_out, and_11_out, and_12_out, and_13_out, and_14_out, and_15_out, and_16_out, and_17_out,
       and_18_out, and_19_out, and_20_out, and_21_out, and_22_out, and_23_out, and_24_out, and_25_out,
       and_26_out, and_27_out, and_28_out, and_29_out, and_30_out, and_31_out, and_32_out, and_33_out,
       and_34_out, and_35_out, and_36_out, and_37_out, and_38_out, and_39_out, and_40_out, and_41_out,
       and_42_out, and_43_out, and_44_out, and_45_out, and_46_out, and_47_out, and_48_out, and_49_out,
       and_50_out, and_51_out, and_52_out, and_53_out, and_54_out, and_55_out, and_56_out, and_57_out,
       and_58_out, and_59_out, and_60_out, and_61_out, and_62_out, and_63_out, and_64_out, and_65_out,
       and_66_out, and_67_out, and_68_out, and_69_out, and_70_out, and_71_out, and_72_out, and_73_out,
       and_74_out, and_75_out, and_76_out, and_77_out, and_78_out, and_79_out, and_80_out, and_81_out,
       and_82_out, and_83_out, and_84_out, and_85_out, and_86_out, and_87_out, and_88_out, and_89_out,
       and_90_out, and_91_out, and_92_out, and_93_out, or_1_out, or_2_out, or_3_out, or_4_out, or_5_out,
       or_6_out, or_7_out, or_8_out, or_9_out, or_10_out, or_11_out, or_12_out, or_13_out, or_14_out,
       or_15_out, or_16_out, or_17_out, or_18_out, or_19_out, or_20_out, or_21_out, or_22_out, or_23_out,
       or_24_out, or_25_out, or_26_out, or_27_out, or_28_out, or_29_out, or_30_out, or_31_out, or_32_out,
       or_33_out, or_34_out, or_35_out, or_36_out, or_37_out, or_38_out, or_39_out, or_40_out, or_41_out,
       or_42_out, or_43_out, or_44_out, or_45_out, or_46_out, or_47_out, or_48_out, or_49_out, or_50_out,
       or_51_out, or_52_out, or_53_out, or_54_out, or_55_out, or_56_out, or_57_out, or_58_out, or_59_out,
       or_60_out, or_61_out, or_62_out, xor_1_out, xor_2_out, xor_3_out, xor_4_out, xor_5_out, xor_6_out,
       xor_7_out, xor_8_out, xor_9_out, xor_10_out, xor_11_out, xor_12_out, xor_13_out, xor_14_out,
       xor_15_out, xor_16_out, xor_17_out, xor_18_out, xor_19_out, xor_20_out, xor_21_out, xor_22_out,
       xor_23_out, xor_24_out, xor_25_out, xor_26_out, xor_27_out, xor_28_out, xor_29_out, xor_30_out,
       xor_31_out, xor_32_out, xor_33_out, xor_34_out, xor_35_out, xor_36_out, xor_37_out, xor_38_out,
       xor_39_out, xor_40_out, xor_41_out, xor_42_out, xor_43_out, xor_44_out, xor_45_out, xor_46_out,
       xor_47_out, xor_48_out, xor_49_out, xor_50_out, xor_51_out, xor_52_out, xor_53_out, xor_54_out,
       xor_55_out, xor_56_out, xor_57_out, xor_58_out, xor_59_out, xor_60_out, xor_61_out, xor_62_out,
       xor_63_out, xor_64_out, xor_65_out, xor_66_out, xor_67_out, xor_68_out, xor_69_out, xor_70_out,
       xor_71_out, xor_72_out, xor_73_out, xor_74_out, xor_75_out, xor_76_out, xor_77_out, xor_78_out,
       xor_79_out, xor_80_out, xor_81_out, xor_82_out, xor_83_out, xor_84_out, xor_85_out, xor_86_out,
       xor_87_out, xor_88_out, xor_89_out, xor_90_out, xor_91_out, xor_92_out, xor_93_out;

  xor xor_1 (xor_1_out, I0, I8);
  and and_1 (and_1_out, I1, I9);
  or or_1 (or_1_out, I2, I10);
  and and_2 (and_2_out, I3, I11);
  xor xor_2 (xor_2_out, I4, I12);
  or or_2 (or_2_out, I5, I13);
  and and_3 (and_3_out, I6, I14);
  xor xor_3 (xor_3_out, I7, I15);
  xor xor_4 (xor_4_out, xor_1_out, and_2_out);
  and and_4 (and_4_out, and_1_out, xor_2_out);
  or or_3 (or_3_out, or_1_out, or_2_out);
  and and_5 (and_5_out, and_2_out, and_3_out);
  xor xor_5 (xor_5_out, xor_2_out, xor_3_out);
  or or_4 (or_4_out, or_2_out, xor_1_out);
  and and_6 (and_6_out, and_3_out, and_1_out);
  xor xor_6 (xor_6_out, xor_3_out, or_1_out);
  xor xor_7 (xor_7_out, xor_4_out, and_5_out);
  and and_7 (and_7_out, and_4_out, xor_5_out);
  or or_5 (or_5_out, or_3_out, or_4_out);
  and and_8 (and_8_out, and_5_out, and_6_out);
  xor xor_8 (xor_8_out, xor_5_out, xor_6_out);
  or or_6 (or_6_out, or_4_out, xor_4_out);
  and and_9 (and_9_out, and_6_out, and_4_out);
  xor xor_9 (xor_9_out, xor_6_out, or_3_out);
  xor xor_10 (xor_10_out, xor_7_out, and_8_out);
  and and_10 (and_10_out, and_7_out, xor_8_out);
  or or_7 (or_7_out, or_5_out, or_6_out);
  and and_11 (and_11_out, and_8_out, and_9_out);
  xor xor_11 (xor_11_out, xor_8_out, xor_9_out);
  or or_8 (or_8_out, or_6_out, xor_7_out);
  and and_12 (and_12_out, and_9_out, and_7_out);
  xor xor_12 (xor_12_out, xor_9_out, or_5_out);
  xor xor_13 (xor_13_out, xor_10_out, and_11_out);
  and and_13 (and_13_out, and_10_out, xor_11_out);
  or or_9 (or_9_out, or_7_out, or_8_out);
  and and_14 (and_14_out, and_11_out, and_12_out);
  xor xor_14 (xor_14_out, xor_11_out, xor_12_out);
  or or_10 (or_10_out, or_8_out, xor_10_out);
  and and_15 (and_15_out, and_12_out, and_10_out);
  xor xor_15 (xor_15_out, xor_12_out, or_7_out);
  xor xor_16 (xor_16_out, xor_13_out, and_14_out);
  and and_16 (and_16_out, and_13_out, xor_14_out);
  or or_11 (or_11_out, or_9_out, or_10_out);
  and and_17 (and_17_out, and_14_out, and_15_out);
  xor xor_17 (xor_17_out, xor_14_out, xor_15_out);
  or or_12 (or_12_out, or_10_out, xor_13_out);
  and and_18 (and_18_out, and_15_out, and_13_out);
  xor xor_18 (xor_18_out, xor_15_out, or_9_out);
  xor xor_19 (xor_19_out, xor_16_out, and_17_out);
  and and_19 (and_19_out, and_16_out, xor_17_out);
  or or_13 (or_13_out, or_11_out, or_12_out);
  and and_20 (and_20_out, and_17_out, and_18_out);
  xor xor_20 (xor_20_out, xor_17_out, xor_18_out);
  or or_14 (or_14_out, or_12_out, xor_16_out);
  and and_21 (and_21_out, and_18_out, and_16_out);
  xor xor_21 (xor_21_out, xor_18_out, or_11_out);
  xor xor_22 (xor_22_out, xor_19_out, and_20_out);
  and and_22 (and_22_out, and_19_out, xor_20_out);
  or or_15 (or_15_out, or_13_out, or_14_out);
  and and_23 (and_23_out, and_20_out, and_21_out);
  xor xor_23 (xor_23_out, xor_20_out, xor_21_out);
  or or_16 (or_16_out, or_14_out, xor_19_out);
  and and_24 (and_24_out, and_21_out, and_19_out);
  xor xor_24 (xor_24_out, xor_21_out, or_13_out);
  xor xor_25 (xor_25_out, xor_22_out, and_23_out);
  and and_25 (and_25_out, and_22_out, xor_23_out);
  or or_17 (or_17_out, or_15_out, or_16_out);
  and and_26 (and_26_out, and_23_out, and_24_out);
  xor xor_26 (xor_26_out, xor_23_out, xor_24_out);
  or or_18 (or_18_out, or_16_out, xor_22_out);
  and and_27 (and_27_out, and_24_out, and_22_out);
  xor xor_27 (xor_27_out, xor_24_out, or_15_out);
  xor xor_28 (xor_28_out, xor_25_out, and_26_out);
  and and_28 (and_28_out, and_25_out, xor_26_out);
  or or_19 (or_19_out, or_17_out, or_18_out);
  and and_29 (and_29_out, and_26_out, and_27_out);
  xor xor_29 (xor_29_out, xor_26_out, xor_27_out);
  or or_20 (or_20_out, or_18_out, xor_25_out);
  and and_30 (and_30_out, and_27_out, and_25_out);
  xor xor_30 (xor_30_out, xor_27_out, or_17_out);
  xor xor_31 (xor_31_out, xor_28_out, and_29_out);
  and and_31 (and_31_out, and_28_out, xor_29_out);
  or or_21 (or_21_out, or_19_out, or_20_out);
  and and_32 (and_32_out, and_29_out, and_30_out);
  xor xor_32 (xor_32_out, xor_29_out, xor_30_out);
  or or_22 (or_22_out, or_20_out, xor_28_out);
  and and_33 (and_33_out, and_30_out, and_28_out);
  xor xor_33 (xor_33_out, xor_30_out, or_19_out);
  xor xor_34 (xor_34_out, xor_31_out, and_32_out);
  and and_34 (and_34_out, and_31_out, xor_32_out);
  or or_23 (or_23_out, or_21_out, or_22_out);
  and and_35 (and_35_out, and_32_out, and_33_out);
  xor xor_35 (xor_35_out, xor_32_out, xor_33_out);
  or or_24 (or_24_out, or_22_out, xor_31_out);
  and and_36 (and_36_out, and_33_out, and_31_out);
  xor xor_36 (xor_36_out, xor_33_out, or_21_out);
  xor xor_37 (xor_37_out, xor_34_out, and_35_out);
  and and_37 (and_37_out, and_34_out, xor_35_out);
  or or_25 (or_25_out, or_23_out, or_24_out);
  and and_38 (and_38_out, and_35_out, and_36_out);
  xor xor_38 (xor_38_out, xor_35_out, xor_36_out);
  or or_26 (or_26_out, or_24_out, xor_34_out);
  and and_39 (and_39_out, and_36_out, and_34_out);
  xor xor_39 (xor_39_out, xor_36_out, or_23_out);
  xor xor_40 (xor_40_out, xor_37_out, and_38_out);
  and and_40 (and_40_out, and_37_out, xor_38_out);
  or or_27 (or_27_out, or_25_out, or_26_out);
  and and_41 (and_41_out, and_38_out, and_39_out);
  xor xor_41 (xor_41_out, xor_38_out, xor_39_out);
  or or_28 (or_28_out, or_26_out, xor_37_out);
  and and_42 (and_42_out, and_39_out, and_37_out);
  xor xor_42 (xor_42_out, xor_39_out, or_25_out);
  xor xor_43 (xor_43_out, xor_40_out, and_41_out);
  and and_43 (and_43_out, and_40_out, xor_41_out);
  or or_29 (or_29_out, or_27_out, or_28_out);
  and and_44 (and_44_out, and_41_out, and_42_out);
  xor xor_44 (xor_44_out, xor_41_out, xor_42_out);
  or or_30 (or_30_out, or_28_out, xor_40_out);
  and and_45 (and_45_out, and_42_out, and_40_out);
  xor xor_45 (xor_45_out, xor_42_out, or_27_out);
  xor xor_46 (xor_46_out, xor_43_out, and_44_out);
  and and_46 (and_46_out, and_43_out, xor_44_out);
  or or_31 (or_31_out, or_29_out, or_30_out);
  and and_47 (and_47_out, and_44_out, and_45_out);
  xor xor_47 (xor_47_out, xor_44_out, xor_45_out);
  or or_32 (or_32_out, or_30_out, xor_43_out);
  and and_48 (and_48_out, and_45_out, and_43_out);
  xor xor_48 (xor_48_out, xor_45_out, or_29_out);
  xor xor_49 (xor_49_out, xor_46_out, and_47_out);
  and and_49 (and_49_out, and_46_out, xor_47_out);
  or or_33 (or_33_out, or_31_out, or_32_out);
  and and_50 (and_50_out, and_47_out, and_48_out);
  xor xor_50 (xor_50_out, xor_47_out, xor_48_out);
  or or_34 (or_34_out, or_32_out, xor_46_out);
  and and_51 (and_51_out, and_48_out, and_46_out);
  xor xor_51 (xor_51_out, xor_48_out, or_31_out);
  xor xor_52 (xor_52_out, xor_49_out, and_50_out);
  and and_52 (and_52_out, and_49_out, xor_50_out);
  or or_35 (or_35_out, or_33_out, or_34_out);
  and and_53 (and_53_out, and_50_out, and_51_out);
  xor xor_53 (xor_53_out, xor_50_out, xor_51_out);
  or or_36 (or_36_out, or_34_out, xor_49_out);
  and and_54 (and_54_out, and_51_out, and_49_out);
  xor xor_54 (xor_54_out, xor_51_out, or_33_out);
  xor xor_55 (xor_55_out, xor_52_out, and_53_out);
  and and_55 (and_55_out, and_52_out, xor_53_out);
  or or_37 (or_37_out, or_35_out, or_36_out);
  and and_56 (and_56_out, and_53_out, and_54_out);
  xor xor_56 (xor_56_out, xor_53_out, xor_54_out);
  or or_38 (or_38_out, or_36_out, xor_52_out);
  and and_57 (and_57_out, and_54_out, and_52_out);
  xor xor_57 (xor_57_out, xor_54_out, or_35_out);
  xor xor_58 (xor_58_out, xor_55_out, and_56_out);
  and and_58 (and_58_out, and_55_out, xor_56_out);
  or or_39 (or_39_out, or_37_out, or_38_out);
  and and_59 (and_59_out, and_56_out, and_57_out);
  xor xor_59 (xor_59_out, xor_56_out, xor_57_out);
  or or_40 (or_40_out, or_38_out, xor_55_out);
  and and_60 (and_60_out, and_57_out, and_55_out);
  xor xor_60 (xor_60_out, xor_57_out, or_37_out);
  xor xor_61 (xor_61_out, xor_58_out, and_59_out);
  and and_61 (and_61_out, and_58_out, xor_59_out);
  or or_41 (or_41_out, or_39_out, or_40_out);
  and and_62 (and_62_out, and_59_out, and_60_out);
  xor xor_62 (xor_62_out, xor_59_out, xor_60_out);
  or or_42 (or_42_out, or_40_out, xor_58_out);
  and and_63 (and_63_out, and_60_out, and_58_out);
  xor xor_63 (xor_63_out, xor_60_out, or_39_out);
  xor xor_64 (xor_64_out, xor_61_out, and_62_out);
  and and_64 (and_64_out, and_61_out, xor_62_out);
  or or_43 (or_43_out, or_41_out, or_42_out);
  and and_65 (and_65_out, and_62_out, and_63_out);
  xor xor_65 (xor_65_out, xor_62_out, xor_63_out);
  or or_44 (or_44_out, or_42_out, xor_61_out);
  and and_66 (and_66_out, and_63_out, and_61_out);
  xor xor_66 (xor_66_out, xor_63_out, or_41_out);
  xor xor_67 (xor_67_out, xor_64_out, and_65_out);
  and and_67 (and_67_out, and_64_out, xor_65_out);
  or or_45 (or_45_out, or_43_out, or_44_out);
  and and_68 (and_68_out, and_65_out, and_66_out);
  xor xor_68 (xor_68_out, xor_65_out, xor_66_out);
  or or_46 (or_46_out, or_44_out, xor_64_out);
  and and_69 (and_69_out, and_66_out, and_64_out);
  xor xor_69 (xor_69_out, xor_66_out, or_43_out);
  xor xor_70 (xor_70_out, xor_67_out, and_68_out);
  and and_70 (and_70_out, and_67_out, xor_68_out);
  or or_47 (or_47_out, or_45_out, or_46_out);
  and and_71 (and_71_out, and_68_out, and_69_out);
  xor xor_71 (xor_71_out, xor_68_out, xor_69_out);
  or or_48 (or_48_out, or_46_out, xor_67_out);
  and and_72 (and_72_out, and_69_out, and_67_out);
  xor xor_72 (xor_72_out, xor_69_out, or_45_out);
  xor xor_73 (xor_73_out, xor_70_out, and_71_out);
  and and_73 (and_73_out, and_70_out, xor_71_out);
  or or_49 (or_49_out, or_47_out, or_48_out);
  and and_74 (and_74_out, and_71_out, and_72_out);
  xor xor_74 (xor_74_out, xor_71_out, xor_72_out);
  or or_50 (or_50_out, or_48_out, xor_70_out);
  and and_75 (and_75_out, and_72_out, and_70_out);
  xor xor_75 (xor_75_out, xor_72_out, or_47_out);
  xor xor_76 (xor_76_out, xor_73_out, and_74_out);
  and and_76 (and_76_out, and_73_out, xor_74_out);
  or or_51 (or_51_out, or_49_out, or_50_out);
  and and_77 (and_77_out, and_74_out, and_75_out);
  xor xor_77 (xor_77_out, xor_74_out, xor_75_out);
  or or_52 (or_52_out, or_50_out, xor_73_out);
  and and_78 (and_78_out, and_75_out, and_73_out);
  xor xor_78 (xor_78_out, xor_75_out, or_49_out);
  xor xor_79 (xor_79_out, xor_76_out, and_77_out);
  and and_79 (and_79_out, and_76_out, xor_77_out);
  or or_53 (or_53_out, or_51_out, or_52_out);
  and and_80 (and_80_out, and_77_out, and_78_out);
  xor xor_80 (xor_80_out, xor_77_out, xor_78_out);
  or or_54 (or_54_out, or_52_out, xor_76_out);
  and and_81 (and_81_out, and_78_out, and_76_out);
  xor xor_81 (xor_81_out, xor_78_out, or_51_out);
  xor xor_82 (xor_82_out, xor_79_out, and_80_out);
  and and_82 (and_82_out, and_79_out, xor_80_out);
  or or_55 (or_55_out, or_53_out, or_54_out);
  and and_83 (and_83_out, and_80_out, and_81_out);
  xor xor_83 (xor_83_out, xor_80_out, xor_81_out);
  or or_56 (or_56_out, or_54_out, xor_79_out);
  and and_84 (and_84_out, and_81_out, and_79_out);
  xor xor_84 (xor_84_out, xor_81_out, or_53_out);
  xor xor_85 (xor_85_out, xor_82_out, and_83_out);
  and and_85 (and_85_out, and_82_out, xor_83_out);
  or or_57 (or_57_out, or_55_out, or_56_out);
  and and_86 (and_86_out, and_83_out, and_84_out);
  xor xor_86 (xor_86_out, xor_83_out, xor_84_out);
  or or_58 (or_58_out, or_56_out, xor_82_out);
  and and_87 (and_87_out, and_84_out, and_82_out);
  xor xor_87 (xor_87_out, xor_84_out, or_55_out);
  xor xor_88 (xor_88_out, xor_85_out, and_86_out);
  and and_88 (and_88_out, and_85_out, xor_86_out);
  or or_59 (or_59_out, or_57_out, or_58_out);
  and and_89 (and_89_out, and_86_out, and_87_out);
  xor xor_89 (xor_89_out, xor_86_out, xor_87_out);
  or or_60 (or_60_out, or_58_out, xor_85_out);
  and and_90 (and_90_out, and_87_out, and_85_out);
  xor xor_90 (xor_90_out, xor_87_out, or_57_out);
  xor xor_91 (xor_91_out, xor_88_out, and_89_out);
  and and_91 (and_91_out, and_88_out, xor_89_out);
  or or_61 (or_61_out, or_59_out, or_60_out);
  and and_92 (and_92_out, and_89_out, and_90_out);
  xor xor_92 (xor_92_out, xor_89_out, xor_90_out);
  or or_62 (or_62_out, or_60_out, xor_88_out);
  and and_93 (and_93_out, and_90_out, and_88_out);
  xor xor_93 (xor_93_out, xor_90_out, or_59_out);
  xor xor_94 (O0, xor_91_out, and_92_out);
  and and_94 (O1, and_91_out, xor_92_out);
  or or_63 (O2, or_61_out, or_62_out);
  and and_95 (O3, and_92_out, and_93_out);
  // XOR_Gate xor_95 has open pins: in0=xor_92_out, in1=xor_93_out, out=open
  // OR_Gate or_64 has open pins: in0=or_62_out, in1=xor_91_out, out=open
  // AND_Gate and_96 has open pins: in0=and_93_out, in1=and_91_out, out=open
  // XOR_Gate xor_96 has open pins: in0=xor_93_out, in1=or_61_out, out=open

  // Notes on the sheet:
  //   256-GATE DIRECT-WIRE STRESS NETLIST
  //   32 LAYERS x 8 GATES
endmodule
